# Fritzing sketch schematic (saved by Fritzing 0.9.6b)
perfboards: 1

parts:
  Part1 = Arduino Nano (Rev3.0) (ICSP)
  MD03A1 = Dual VNH2SP30 Motor Driver [part_number=MD03A]
  M1 = RioRand LM2596
  Enc1 = shaft encoder
  Enc2 = shaft encoder
  BAT1 = LIPO-2000mAh [package=lipo-2000]
  J1 = Basic Servo
  M2 = DC Motor

nets:
  GND: Part1.GND, MD03A1.GND, M1.Pin_4
  N1: Part1.D2, Enc2.OUT
  N2: Part1.D3, Enc1.OUT
  N3: Part1.D6, J1.pulse
  N4: Part1.D9, MD03A1.PWM
  N5: Part1.D10, MD03A1.1INb
  N6: Part1.D12/MISO, MD03A1.1INa
  VIN: Part1.VIN, M1.Pin_3, J1.vcc
  N7: Part1.5V, MD03A1.+5V_(IN)
  N8: MD03A1.OUT_1A, M2.pin_2
  N9: MD03A1.OUT_1B, M2.pin_1
  N10: M1.Pin_1, BAT1.+
  N11: M1.Pin_2, BAT1.-
  VCC: Enc1.VCC, Enc2.VCC
  GND_2: Enc1.GND, Enc2.GND, J1.gnd
